# Fritzing sketch circuit (saved by Fritzing 0.9.4)

parts:
  Keypad4x4 = Keypad Membran 4x4
  R1 = Resistor [tolerance=±5% resistance=330 package=THT]
  LED1 = LED - 3mm [color="Red (635nm)" package="3 mm [THT]"]
  LED2 = LED - 3mm [color="Red (635nm)" package="3 mm [THT]"]
  LED3 = LED - 3mm [color="Red (635nm)" package="3 mm [THT]"]
  LED4 = LED - 3mm [color="Red (635nm)" package="3 mm [THT]"]
  Switch = Toggle Switch [package=THT]
  Bauteil1 = Arduino Nano (Rev3.0)

nets:
  N1: Keypad4x4.Pin1, Bauteil1.D8
  N2: Keypad4x4.Pin2, Bauteil1.D7
  N3: Keypad4x4.Pin3, Bauteil1.D6
  N4: Keypad4x4.Pin4, Bauteil1.D5
  N5: Keypad4x4.Pin5, Bauteil1.A0
  N6: Keypad4x4.Pin6, Bauteil1.A1
  N7: Keypad4x4.Pin7, Bauteil1.A2
  N8: Keypad4x4.Pin8, Bauteil1.A3
  N9: R1.Pin_0, Bauteil1.GND
  N10: R1.Pin_1, Switch.L1
  N11: LED1.cathode, LED2.cathode, LED3.cathode, LED4.cathode, Switch.COM
  N12: LED1.anode, Bauteil1.D11/MOSI
  N13: LED2.anode, Bauteil1.D10
  N14: LED3.anode, Bauteil1.D9
  N15: LED4.anode, Bauteil1.D3

custom parts:
  Keypad Membran 4x4: Membrane Keypad 4x4 Matrix
